// Logisim project Lecture02.circ as structural Verilog: 2 circuits, main circuit ALU
module ALU (
  input  [15:0] x,
  input  zx,
  input  nx,
  input  [15:0] y,
  input  zy,
  input  ny,
  input  f,
  input  no,
  output [15:0] out,
  output ng,
  output zr
);

  wire [15:0] adder_1_out, and_1_out, and_2_out, and_3_out, and_4_out, and_5_out, bit_extender_1_out,
       bit_extender_2_out, bit_extender_3_out, bit_extender_4_out, bit_extender_5_out, bit_extender_6_out,
       or_1_out, xor_1_out, xor_2_out;

  assign bit_extender_1_out = {{15{zx}}, zx};  // Bit_Extender bit_extender_1
  assign bit_extender_2_out = {{15{nx}}, nx};  // Bit_Extender bit_extender_2
  assign bit_extender_3_out = {{15{zy}}, zy};  // Bit_Extender bit_extender_3
  assign bit_extender_4_out = {{15{ny}}, ny};  // Bit_Extender bit_extender_4
  assign bit_extender_5_out = {{15{f}}, f};  // Bit_Extender bit_extender_5
  assign bit_extender_6_out = {{15{no}}, no};  // Bit_Extender bit_extender_6
  assign and_1_out = x & ~bit_extender_1_out;  // AND_Gate and_1, 16 bits wide
  assign and_2_out = y & ~bit_extender_3_out;  // AND_Gate and_2, 16 bits wide
  assign xor_1_out = and_1_out ^ bit_extender_2_out;  // XOR_Gate xor_1, 16 bits wide
  assign xor_2_out = and_2_out ^ bit_extender_4_out;  // XOR_Gate xor_2, 16 bits wide
  Adder #(.width(16)) adder_1 (.a(xor_1_out), .b(xor_2_out), .out(adder_1_out));  // open: cin, cout
  assign and_3_out = xor_1_out & xor_2_out;  // AND_Gate and_3, 16 bits wide
  assign and_4_out = adder_1_out & bit_extender_5_out;  // AND_Gate and_4, 16 bits wide
  assign and_5_out = ~bit_extender_5_out & and_3_out;  // AND_Gate and_5, 16 bits wide
  assign or_1_out = and_4_out | and_5_out;  // OR_Gate or_1, 16 bits wide
  assign out = or_1_out ^ bit_extender_6_out;  // XOR_Gate xor_3, 16 bits wide
  Comparator16 comparator16_1 (.ng(ng), .zr(zr), .in_1(out));

  // Notes on the sheet:
  //   w1
  //   w3
  //   w2
  //   w4
  //   and
  //   sum
  //   w5
  //   w6
  //   w7
  //   w8
endmodule

module Comparator16 (
  input  [15:0] in_1,
  output ng,
  output zr
);

  wire and_1_out, and_2_out, and_3_out, and_4_out, and_5_out, and_6_out, and_7_out, and_8_out, and_9_out,
       and_10_out, and_11_out, and_12_out, and_13_out, and_14_out;
  wire [15:0] not_1_out;

  and and_1 (and_1_out, not_1_out[13], not_1_out[12]);
  and and_2 (and_2_out, not_1_out[15], not_1_out[14]);
  assign not_1_out = ~in_1;  // NOT_Gate not_1, 16 bits wide
  and and_3 (and_3_out, not_1_out[11], not_1_out[10]);
  and and_4 (and_4_out, not_1_out[9], not_1_out[8]);
  and and_5 (and_5_out, not_1_out[7], not_1_out[6]);
  and and_6 (and_6_out, not_1_out[3], not_1_out[2]);
  and and_7 (and_7_out, not_1_out[5], not_1_out[4]);
  and and_8 (and_8_out, not_1_out[1], not_1_out[0]);
  and and_9 (and_9_out, and_8_out, and_6_out);
  and and_10 (and_10_out, and_7_out, and_5_out);
  and and_11 (and_11_out, and_4_out, and_3_out);
  and and_12 (and_12_out, and_1_out, and_2_out);
  and and_13 (and_13_out, and_9_out, and_10_out);
  and and_14 (and_14_out, and_11_out, and_12_out);
  and and_15 (zr, and_13_out, and_14_out);

  assign ng = in_1[15];
endmodule
